// Logisim project Moltiplicatore.circ as structural Verilog: 12 circuits, main circuit main
module arithmetic_unit (
  input  [15:0] Prod,
  input  [7:0] Multiplicand,
  output [15:0] newProd
);

  wire multiplexer_2_out, n8_bit_adder_1_cout;
  wire [7:0] n8_bit_adder_1_sum;
  wire [15:0] multiplexer_1_out;

  _8_bit_adder u_8_bit_adder_1 (.A(Prod[15:8]), .B(Multiplicand), .Sum(n8_bit_adder_1_sum), .Cout(n8_bit_adder_1_cout));
  Multiplexer #(.width(16), .enable("false")) multiplexer_1 (
    .in0(Prod), .in1({n8_bit_adder_1_sum, Prod[7:0]}), .out(multiplexer_1_out), .sel(Prod[0]));
  Multiplexer #(.enable("false")) multiplexer_2 (
    .in0(1'b0), .in1(n8_bit_adder_1_cout), .out(multiplexer_2_out), .sel(Prod[0]));
  shifter shifter_1 (.A(multiplexer_1_out), .n(multiplexer_2_out), .B(newProd));
endmodule

module _1_bit_adder (
  input  A,
  input  B,
  input  Cin,
  output Sum,
  output Cout
);

  wire and_1_out, and_2_out, xor_1_out;

  xor xor_1 (xor_1_out, A, B);
  xor xor_2 (Sum, xor_1_out, Cin);
  and and_1 (and_1_out, Cin, xor_1_out);
  and and_2 (and_2_out, A, B);
  or or_1 (Cout, and_1_out, and_2_out);
endmodule

module _2_bit_adder (
  input  Cin,
  input  [1:0] A,
  input  [1:0] B,
  output [1:0] Sum,
  output Cout
);

  wire n1_bit_adder_1_cout;

  _1_bit_adder u_1_bit_adder_1 (.A(A[0]), .B(B[0]), .Cin(Cin), .Cout(n1_bit_adder_1_cout), .Sum(Sum[0]));
  _1_bit_adder u_1_bit_adder_2 (.A(A[1]), .B(B[1]), .Cin(n1_bit_adder_1_cout), .Cout(Cout), .Sum(Sum[1]));
endmodule

module _8_bit_adder (
  input  [7:0] A,
  input  [7:0] B,
  output [7:0] Sum,
  output Cout
);

  wire n2_bit_adder_1_cout, n2_bit_adder_2_cout, n2_bit_adder_3_cout;

  _2_bit_adder u_2_bit_adder_1 (.A(A[1:0]), .B(B[1:0]), .Sum(Sum[1:0]), .Cout(n2_bit_adder_1_cout), .Cin(1'b0));
  _2_bit_adder u_2_bit_adder_2 (
    .A(A[3:2]), .B(B[3:2]), .Sum(Sum[3:2]), .Cout(n2_bit_adder_2_cout), .Cin(n2_bit_adder_1_cout));
  _2_bit_adder u_2_bit_adder_3 (
    .A(A[5:4]), .B(B[5:4]), .Sum(Sum[5:4]), .Cout(n2_bit_adder_3_cout), .Cin(n2_bit_adder_2_cout));
  _2_bit_adder u_2_bit_adder_4 (.A(A[7:6]), .B(B[7:6]), .Sum(Sum[7:6]), .Cout(Cout), .Cin(n2_bit_adder_3_cout));
endmodule

module extender (
  input  [7:0] A,
  output [15:0] ExtA
);


  assign ExtA = {{8{1'b0}}, A};
endmodule

module overflow_check (
  input  [15:0] ProdUnsigned,
  output Overflow
);

  wire comparator_1_eq, comparator_1_gt, comparator_2_eq, comparator_2_gt;

  Comparator #(.width(16), .mode("unsigned")) comparator_1 (
    .a(ProdUnsigned), .b(16'h80), .gt(comparator_1_gt), .eq(comparator_1_eq));  // open: lt
  Comparator #(.mode("unsigned")) comparator_2 (
    .a(ProdUnsigned[7:0]), .b(8'h80), .gt(comparator_2_gt), .eq(comparator_2_eq));  // open: lt
  or or_1 (Overflow, comparator_1_gt, comparator_1_eq, comparator_2_gt, comparator_2_eq);
endmodule

module counter (
  input  Reset,
  input  Clk,
  output Started,
  output Ongoing
);

  wire and_1_out, counter_1_carry;
  wire [3:0] counter_1_q;

  Counter #(.width(4), .max('h8), .ongoal("continue")) counter_1 (
    .Q(counter_1_q), .carry(counter_1_carry), .clk(and_1_out), .clr(Reset));  // open: load, D, count
  and and_1 (and_1_out, Clk, Ongoing);
  not not_1 (Ongoing, counter_1_carry);
  Comparator #(.width(4)) comparator_1 (.a(4'b0000), .b(counter_1_q), .lt(Started));  // open: gt, eq
endmodule

module complementer (
  input  [7:0] A,
  output [7:0] R
);

  wire [7:0] not_1_out;

  assign not_1_out = ~A;  // NOT_Gate not_1, 8 bits wide
  _8_bit_adder u_8_bit_adder_1 (.A(not_1_out), .B(8'h1), .Sum(R));  // open: Cout
endmodule

module shifter (
  input  [15:0] A,
  input  n,
  output [15:0] B
);


  assign B = {n, A[15:1]};
endmodule

module multiplier (
  input  [7:0] Multiplier,
  input  Clk,
  input  Reset,
  input  [7:0] Multiplicand,
  output Overflow,
  output [15:0] ProdUnsigned,
  output [7:0] ProdSigned,
  output ProdSign
);

  wire counter_1_ongoing, counter_1_started;
  wire [15:0] extender_1_exta, multiplexer_1_out, register_1_q;

  extender extender_1 (.A(Multiplier), .ExtA(extender_1_exta));
  Multiplexer #(.width(16), .enable("false")) multiplexer_1 (
    .in0(extender_1_exta), .in1({ProdUnsigned[15:8], ProdSigned}), .out(multiplexer_1_out),
    .sel(counter_1_started));
  counter counter_1 (.Ongoing(counter_1_ongoing), .Started(counter_1_started), .Clk(Clk), .Reset(Reset));
  Register #(.width(16)) register_1 (
    .D(multiplexer_1_out), .en(counter_1_ongoing), .Q(register_1_q), .clk(Clk), .clr(Reset));
  arithmetic_unit arithmetic_unit_1 (
    .Prod(register_1_q), .Multiplicand(Multiplicand), .newProd({ProdUnsigned[15:8], ProdSigned}));
  xnor xnor_1 (ProdSign, Multiplicand[7], Multiplier[7]);
  overflow_check overflow_check_1 (.ProdUnsigned({ProdUnsigned[15:8], ProdSigned}), .Overflow(Overflow));

  assign ProdUnsigned[7:0] = ProdSigned;
endmodule

module main (
  input  [7:0] Multiplier,
  input  [7:0] Multiplicand,
  output Overflow,
  output Positive,
  output [15:0] ProdUnsigned,
  output [7:0] ProdSigned
);

  wire clock_1_out, Restart_out;

  multiplier multiplier_1 (
    .Multiplier(Multiplier), .Reset(Restart_out), .Clk(clock_1_out), .Multiplicand(Multiplicand),
    .ProdSign(Positive), .Overflow(Overflow), .ProdUnsigned(ProdUnsigned), .ProdSigned(ProdSigned));
  Clock clock_1 (.out(clock_1_out));
  Button Restart (.out(Restart_out));
endmodule

module abs (
  input  [7:0] in_1,
  output [7:0] out_2
);

  wire [7:0] complementer_1_r;

  complementer complementer_1 (.A(in_1), .R(complementer_1_r));
  Multiplexer #(.width(8), .enable("false")) multiplexer_1 (
    .in0(in_1), .in1(complementer_1_r), .out(out_2), .sel(in_1[7]));
endmodule
